# Fritzing sketch QuizBoard (saved by Fritzing 0.8.7b)
circuit board: 16.2687cm x 9.75771cm
breadboards: 2

parts:
  Part1 = Arduino Micro (Rev3)
  Part2 = Bluetooth Mate Silver
  Audio_Module1 = Audio Module
  R1 = Resistor [tolerance=±5% resistance=1M package=THT]
  C1 = Ceramic Capacitor [capacitance=100nF package="100 mil [THT, multilayer]"]
  J1 = Piezo Speaker
  Power_plug1 = Power plug
  Part3 = LED Matrix - Serial Interface - Red/Green/Blue
  U1 = 74HC4067 [package=ssop24]
  U2 = 3.5mm Audio Jack [package=audio-jack-3.5mm-smd]

nets:
  N1: Part1.D1/TX, Part2.RX_5V
  N2: Part1.D0/RX, Part2.TX_5V
  GND: Part1.GND, Part2.GND, Audio_Module1.GND, C1.1, J1.pin1, Power_plug1.GND, Part3.GND, U1.GND, U1.EN
  N3: Part1.D2/SDA, R1.Pin_0, C1.0, U1.COM
  N4: Part1.D3/SCL, J1.pin2
  N5: Part1.D4_PWM/A6, R1.Pin_1
  N6: Part1.D5_PWM, U1.S3
  N7: Part1.D6_PWM/A7, U1.S2
  N8: Part1.D7, U1.S1
  N9: Part1.D8_PWM/A8, U1.S0
  N10: Part1.D9_PWM/A9, Audio_Module1.DCLK
  N11: Part1.D10_PWM/A10, Audio_Module1.DIN
  N12: Part1.D11_PWM, Audio_Module1.BUSY
  N13: Part1.D12_PWM/A11, Audio_Module1.RESET
  VIN: Part1.VIN, Power_plug1.VCC
  5V: Part1.5V, Part2.VCC, Part3.VCC, U1.VCC
  N14: Part1.A2, Part3.SCK
  N15: Part1.A1, Part3.CS
  N16: Part1.A0, Part3.MISO
  3.3V: Audio_Module1.3.3V
  N17: Audio_Module1.SPK+, U2.SLEEVE
  N18: Audio_Module1.SPK-, U2.RIGHT, U2.LEFT

notes:
  LED matrix MAX7219
  Arduino Micro Based Quiz Board .
  External Sound system can connect here for .ad4 sounds
  Blutooth module to pass results so next device and also set new Queation and answer parameter
  Multiplexer for extra pins
  Buzzer for different tone
  Left Touch Pins
  Right Touch Pins
  QuizBoardV1, Makes Capacitive Quizboard by Sanjeet Raj Pandey, 1

custom parts:
  Audio Module: SparkFun's small audio playback module, WIG-11125. Plays back sounds from a microSD card.
